# Fritzing sketch action potential (saved by Fritzing 0.9.2b)
breadboards: 8

parts:
  Part1 = Arduino Uno (Rev3)
  U1 = 74HC595 [package="DIP16 [THT]"]
  U2 = 74HC595 [package="DIP16 [THT]"]
  C1 = Capacitor [package=cap-pth-small2]
  R1 = Resistor [tolerance=±5% resistance=330 package="0402 [SMD]"]
  R2 = Resistor [tolerance=±5% resistance=330 package="0402 [SMD]"]
  R3 = Resistor [tolerance=±5% resistance=330 package="0402 [SMD]"]
  R4 = Resistor [tolerance=±5% resistance=330 package="0402 [SMD]"]
  R5 = Resistor [tolerance=±5% resistance=330 package="0402 [SMD]"]
  R6 = Resistor [tolerance=±5% resistance=330 package="0402 [SMD]"]
  R7 = Resistor [tolerance=±5% resistance=330 package="0402 [SMD]"]
  R8 = Resistor [tolerance=±5% resistance=330 package="0402 [SMD]"]
  R9 = Resistor [tolerance=±5% resistance=330 package="0402 [SMD]"]
  R10 = Resistor [tolerance=±5% resistance=330 package="0402 [SMD]"]
  R11 = Resistor [tolerance=±5% resistance=330 package="0402 [SMD]"]
  R12 = Resistor [tolerance=±5% resistance=330 package="0402 [SMD]"]
  LED1 = RGB LED (com. anode, rbg) [package="5 mm [THT]"]
  LED2 = smd LED [color="Red (633nm)" package="1206 [SMD]"]
  LED3 = smd LED [color="Blue (505nm)" package="1206 [SMD]"]
  LED4 = smd LED [color="Green (565nm)" package="1206 [SMD]"]
  LED5 = smd LED [color="Green (565nm)" package="1206 [SMD]"]
  LED6 = smd LED [color="Blue (505nm)" package="1206 [SMD]"]
  LED7 = smd LED [color="Red (633nm)" package="1206 [SMD]"]
  LED8 = smd LED [color="Green (565nm)" package="1206 [SMD]"]
  LED9 = smd LED [color="Blue (505nm)" package="1206 [SMD]"]
  LED10 = smd LED [color="Red (633nm)" package="1206 [SMD]"]
  LED11 = smd LED [color="Green (565nm)" package="1206 [SMD]"]
  LED12 = smd LED [color="Blue (505nm)" package="1206 [SMD]"]
  LED13 = smd LED [color="Red (633nm)" package="1206 [SMD]"]
  R13 = Resistor [tolerance=±5% resistance=330 package="0402 [SMD]"]
  R14 = Resistor [tolerance=±5% resistance=330 package="0402 [SMD]"]
  R15 = Resistor [tolerance=±5% resistance=330 package="0402 [SMD]"]
  S1 = Pushbutton [package="[THT]"]
  R16 = Resistor [tolerance=±5% resistance=330 package="0402 [SMD]"]
  LED14 = smd LED [color="Red (633nm)" package="1206 [SMD]"]

nets:
  N1: Part1.D8, R14.Pin_1
  N2: Part1.D9_PWM, U1.ST_CP, U2.ST_CP, C1.2
  N3: Part1.D11_PWM/MOSI, U2.DS
  N4: Part1.D12/MISO, U1.SH_CP, U2.SH_CP
  N5: Part1.D13/SCK, LED14.anode
  VCC: Part1.D3_PWM, Part1.5V, U1.Q7', U1.MR, U1.VCC, U2.MR, U2.VCC, C1.1, S1.Pin_1, S1.Pin_2, S1.Pin_3, S1.Pin_4, R16.Pin_0
  N6: Part1.D6_PWM, R13.Pin_1
  N7: Part1.D7, R15.Pin_1
  N8: Part1.VIN, U1.OE, U2.OE, LED1.common_anode, LED2.cathode, LED3.cathode, LED4.cathode, LED5.cathode, LED6.cathode, LED7.cathode, LED8.cathode, LED9.cathode, LED10.cathode, LED11.cathode, LED12.cathode, LED13.cathode, R16.Pin_1, LED14.cathode
  N9: U1.Q1, R10.Pin_1
  N10: U1.Q2, R11.Pin_1
  N11: U1.Q3, R12.Pin_1
  N12: U1.DS, U2.Q7'
  N13: U1.Q0, R9.Pin_1
  N14: U2.Q1, R2.Pin_1
  N15: U2.Q2, R6.Pin_1
  N16: U2.Q3, R3.Pin_1
  N17: U2.Q4, R4.Pin_1
  N18: U2.Q5, R5.Pin_1
  N19: U2.Q6, R7.Pin_1
  N20: U2.Q7, R8.Pin_1
  N21: U2.Q0, R1.Pin_1
  N22: R1.Pin_0, LED13.anode
  N23: R2.Pin_0, LED11.anode
  N24: R3.Pin_0, LED12.anode
  N25: R4.Pin_0, LED10.anode
  N26: R5.Pin_0, LED8.anode
  N27: R6.Pin_0, LED9.anode
  N28: R7.Pin_0, LED7.anode
  N29: R8.Pin_0, LED5.anode
  N30: R9.Pin_0, LED6.anode
  N31: R10.Pin_0, LED2.anode
  N32: R11.Pin_0, LED4.anode
  N33: R12.Pin_0, LED3.anode
  N34: LED1.red_cathode, R13.Pin_0
  N35: LED1.blue_cathode, R14.Pin_0
  N36: LED1.green_cathode, R15.Pin_0
